// Digital circuit Punto1.dig as structural Verilog
module Punto1 (
  input  _01,
  input  _02,
  input  _03,
  input  D1,
  input  D2,
  input  D3,
  input  D4,
  input  D5,
  input  D6,
  input  D7,
  input  D8,
  output Output
);

  wire and_1_out, and_2_out, and_3_out, and_4_out, and_5_out, and_6_out, and_7_out, and_8_out, not_1_out,
       not_2_out, not_3_out, or_1_out, or_2_out;

  not not_1 (not_1_out, _01);
  not not_2 (not_2_out, _02);
  not not_3 (not_3_out, _03);
  and and_1 (and_1_out, D1, _01, _02, _03);
  and and_2 (and_2_out, D2, _01, _02, not_3_out);
  and and_3 (and_3_out, D3, _01, not_2_out, not_3_out);
  and and_4 (and_4_out, D4, _01, not_2_out, _03);
  and and_5 (and_5_out, D5, not_1_out, not_2_out, _03);
  and and_6 (and_6_out, D6, not_1_out, _02, _03);
  and and_7 (and_7_out, D7, not_1_out, _02, not_3_out);
  and and_8 (and_8_out, D8, not_1_out, not_2_out, not_3_out);
  or or_1 (or_1_out, and_1_out, and_2_out, and_3_out, and_4_out);
  or or_2 (or_2_out, and_5_out, and_6_out, and_7_out, and_8_out);
  or or_3 (Output, or_1_out, or_2_out);

  // Notes on the sheet:
  //   PUNTO 1
  //   Multiplexor de 8 entradas (D1, D2, D3, D4, D5, D6, D7, D8)
  //   La seleccion de entradas se hace con los inputs 01, 02 y 03
endmodule
