// Digital circuit Punto2.dig as structural Verilog
module Punto2 (
  input  _01,
  input  _02,
  input  D1,
  output Output_1,
  output Output_2,
  output Output_3,
  output Output_4
);

  wire not_1_out, not_2_out;

  not not_1 (not_1_out, _01);
  not not_2 (not_2_out, _02);
  and and_1 (Output_1, D1, _01, _02);
  and and_2 (Output_2, D1, _01, not_2_out);
  and and_3 (Output_3, D1, not_1_out, _02);
  and and_4 (Output_4, D1, not_1_out, not_2_out);

  // Notes on the sheet:
  //   PUNTO 2
  //   Demultiplexor de 1 entradas (D1) y 4 salidas (Output 1,2,3,4)
  //   La seleccion de salidas se hace con los inputs 01 y 02
endmodule
