// Digital circuit Punto3.dig as structural Verilog
module Punto3 (
  input  Set,
  input  Reset,
  input  clk,
  input  J,
  input  K,
  input  clk_2,
  input  in_10,
  input  clk_3,
  input  in_12,
  output Q,
  output Q_2,
  output Q_3,
  output out_13,
  output out_14,
  output Q_4
);

  wire nand_1_out, nand_2_out, nand_3_out, nand_4_out, nand_5_out, nand_6_out, nand_9_out, nand_10_out,
       nand_11_out, nand_12_out, nand_13_out, nand_14_out, not_1_out, not_2_out;

  not not_1 (not_1_out, clk_2);
  nand nand_1 (nand_1_out, Set, not_1_out);
  nand nand_2 (nand_2_out, not_1_out, Reset);
  nand nand_3 (nand_3_out, nand_1_out, nand_4_out);
  nand nand_4 (nand_4_out, nand_3_out, nand_2_out);
  nand nand_5 (nand_5_out, nand_3_out, clk_2);
  nand nand_6 (nand_6_out, clk_2, nand_4_out);
  nand nand_7 (Q, nand_5_out, Q_2);
  nand nand_8 (Q_2, Q, nand_6_out);
  nand nand_9 (nand_9_out, Q_4, J, clk);
  nand nand_10 (nand_10_out, clk, K, Q_3);
  nand nand_11 (nand_11_out, nand_9_out, nand_12_out);
  nand nand_12 (nand_12_out, nand_11_out, nand_10_out);
  RS_FF rs_ff_1 (.S(in_10), .C(clk_3), .R(in_12), .Q(out_13), .nQ(out_14));
  not not_2 (not_2_out, clk);
  nand nand_13 (nand_13_out, nand_11_out, not_2_out);
  nand nand_14 (nand_14_out, not_2_out, nand_12_out);
  nand nand_15 (Q_3, nand_13_out, Q_4);
  nand nand_16 (Q_4, Q_3, nand_14_out);

  // Other names for the same wires on the sheet: Clock = clk; ClockRS = clk_2

  // Notes on the sheet:
  //   Punto 3
  //   RS FLip-FLop
  //   El Flip-Flop JK, fue diseñado para solucionar el error que tenía el Flip-Flop RS con la oscilación al
  //   activar el Reset y el Set al mismo tiempo.
  //   Este Flip-Flop también trabaja con dos entradas (J y K) y tiene dos salidas (Q Y Q').
  //   Entonces, cada que activemos la entrada J y se cumpla un ciclo de reloj, se activara la señal Q;
  //   ahora, cuando se activa la señal K, es como si activáramos el Reset en el Flip-Flop RS, es decir
  //   se apaga la salida Q y se activa Q´, esto ocurre con la señal de Reloj.
  //   Ahora, cuando se activan tanto J como K, comienza a saltar entre las salidas, es decir,
  //   pasa de Q a Q' con cada cambio en la señal de reloj, y el sistema no nos presenta ningún error
  //   debido a esta oscilación.
  //   En los dos Flip-Flops, cada que prendemos un input, la configuración de salida será la misma, hasta
  //   cuando no halla un cambio en los inputs, es decir, en el caso del RS, si prendo el Set, y activo la
  //   señal de reloj, este prenderá el output Q y Q' seguirá apagado, esta configuración de salida
  //   seguirá igual hasta que apeguemos el Set, prendamos Reset y esperemos otro ciclo de reloj, así
  //   la configuración de salida será igual, incluso si se apaga el set y solo cambiará al hacer lo anterior.
  //   JK FLip-FLop
  //   Este Flip-Flop, tiene dos entradas, que son un Reset y un Set, y dos salidas, una
  //   de ellas Q y la otra Q' (Negación de Q). Las entradas Set (R) y Reset(R), nos
  //   permiten activar una entrada o la otra, este cambio se da con ayuda de la
  //   señal de reloj, al activar el Set y dar un cambio en la señal de reloj, se activara
  //   la salida Q y apagara la Q', en el caso del reset y al pasar la señal de reloj,
  //   se activa la salida Q' y se desactiva Q.
  //   Digital cuenta con Flip-Flop RS con señal de reloj, al utilizarlo podemos observar
  //   que funciona muy parecido al que construimos con compuertas NAND, pero tiene una
  //   particularidad, cuando se activan tanto el set como el reset, las salidas comienzan a oscilar
  //   de manera aleatoria entre ellas, mientras que el Flip-Flop con compuertas NAND, este
  //   comportamiento no se da, sino que el sistema nos manda un error de oscilación.
  //   Fli-FLop RS en DIgital
endmodule
