// Digital circuit Punto4.dig as structural Verilog
module Punto4 (
  input  Set,
  input  Enable,
  input  Clear,
  input  D3,
  input  D2,
  input  D1,
  input  D0,
  input  in_9,
  input  Set_2,
  input  in_11,
  input  Set_3,
  input  Clock,
  input  in_16,
  input  Set_4,
  input  in_18,
  input  Set_5,
  input  in_22,
  input  Set_6,
  input  in_24,
  input  Set_7,
  input  in_28,
  input  Set_8,
  input  in_30,
  input  Set_9,
  output Out_3,
  output Out_3a,
  output Out_2,
  output Out_2a,
  output Out_1,
  output Out_1a,
  output Out_0,
  output Out_0a
);

  wire D0_t, D1_t, D2_t, D3_t, d_ff_as_1_q, d_ff_as_6_q, d_ff_as_9_q, d_ff_as_11_q, driver_1_out,
       driver_2_out, driver_3_out, driver_4_out, multiplexer_1_out, multiplexer_2_out, multiplexer_3_out,
       multiplexer_4_out, multiplexer_5_out, multiplexer_6_out, multiplexer_7_out, multiplexer_8_out,
       multiplexer_9_out, multiplexer_10_out, multiplexer_11_out, multiplexer_12_out;

  assign Out_3 = ~D3_t ? d_ff_as_1_q : 1'bz;  // DriverInvSel driverinvsel_1
  assign driver_1_out = D3_t ? in_9 : 1'bz;  // Driver driver_1
  Multiplexer multiplexer_1 (.sel(Enable), .in_0(Out_3a), .in_1(driver_1_out), .out(multiplexer_1_out));
  D_FF_AS d_ff_as_1 (.Set(Set_2), .D(multiplexer_3_out), .C(Clock), .Clr(Clear), .Q(d_ff_as_1_q));  // open: nQ
  D_FF_AS d_ff_as_2 (.Set(Set_3), .D(multiplexer_1_out), .C(Clock), .Clr(Clear), .Q(Out_3a));  // open: nQ
  Multiplexer multiplexer_2 (.sel(Enable), .in_0(D3_t), .in_1(D3), .out(multiplexer_2_out));
  Multiplexer multiplexer_3 (.sel(Enable), .in_0(d_ff_as_1_q), .in_1(in_11), .out(multiplexer_3_out));
  D_FF_AS d_ff_as_3 (.Set(Set), .D(multiplexer_2_out), .C(Clock), .Clr(Clear), .Q(D3_t));  // open: nQ
  Multiplexer multiplexer_4 (.sel(Enable), .in_0(D2_t), .in_1(D2), .out(multiplexer_4_out));
  D_FF_AS d_ff_as_4 (.Set(Set), .D(multiplexer_4_out), .C(Clock), .Clr(Clear), .Q(D2_t));  // open: nQ
  assign Out_2 = ~D2_t ? d_ff_as_6_q : 1'bz;  // DriverInvSel driverinvsel_2
  assign driver_2_out = D2_t ? in_16 : 1'bz;  // Driver driver_2
  Multiplexer multiplexer_5 (.sel(Enable), .in_0(D1_t), .in_1(D1), .out(multiplexer_5_out));
  D_FF_AS d_ff_as_5 (.Set(Set), .D(multiplexer_5_out), .C(Clock), .Clr(Clear), .Q(D1_t));  // open: nQ
  Multiplexer multiplexer_6 (.sel(Enable), .in_0(Out_2a), .in_1(driver_2_out), .out(multiplexer_6_out));
  Multiplexer multiplexer_7 (.sel(Enable), .in_0(D0_t), .in_1(D0), .out(multiplexer_7_out));
  D_FF_AS d_ff_as_6 (.Set(Set_4), .D(multiplexer_8_out), .C(Clock), .Clr(Clear), .Q(d_ff_as_6_q));  // open: nQ
  D_FF_AS d_ff_as_7 (.Set(Set), .D(multiplexer_7_out), .C(Clock), .Clr(Clear), .Q(D0_t));  // open: nQ
  Multiplexer multiplexer_8 (.sel(Enable), .in_0(d_ff_as_6_q), .in_1(in_18), .out(multiplexer_8_out));
  D_FF_AS d_ff_as_8 (.Set(Set_5), .D(multiplexer_6_out), .C(Clock), .Clr(Clear), .Q(Out_2a));  // open: nQ
  assign Out_0 = ~D0_t ? d_ff_as_9_q : 1'bz;  // DriverInvSel driverinvsel_3
  assign driver_3_out = D0_t ? in_28 : 1'bz;  // Driver driver_3
  Multiplexer multiplexer_9 (.sel(Enable), .in_0(Out_0a), .in_1(driver_3_out), .out(multiplexer_9_out));
  assign Out_1 = ~D1_t ? d_ff_as_11_q : 1'bz;  // DriverInvSel driverinvsel_4
  assign driver_4_out = D1_t ? in_22 : 1'bz;  // Driver driver_4
  D_FF_AS d_ff_as_9 (.Set(Set_8), .D(multiplexer_11_out), .C(Clock), .Clr(Clear), .Q(d_ff_as_9_q));  // open: nQ
  D_FF_AS d_ff_as_10 (.Set(Set_9), .D(multiplexer_9_out), .C(Clock), .Clr(Clear), .Q(Out_0a));  // open: nQ
  Multiplexer multiplexer_10 (.sel(Enable), .in_0(Out_1a), .in_1(driver_4_out), .out(multiplexer_10_out));
  Multiplexer multiplexer_11 (.sel(Enable), .in_0(d_ff_as_9_q), .in_1(in_30), .out(multiplexer_11_out));
  D_FF_AS d_ff_as_11 (.Set(Set_6), .D(multiplexer_12_out), .C(Clock), .Clr(Clear), .Q(d_ff_as_11_q));  // open: nQ
  D_FF_AS d_ff_as_12 (.Set(Set_7), .D(multiplexer_10_out), .C(Clock), .Clr(Clear), .Q(Out_1a));  // open: nQ
  Multiplexer multiplexer_12 (.sel(Enable), .in_0(d_ff_as_11_q), .in_1(in_24), .out(multiplexer_12_out));

  // Notes on the sheet:
  //   in_9: default 1
  //   in_11: default 1
  //   in_16: default 1
  //   in_18: default 1
  //   in_22: default 1
  //   in_24: default 1
  //   in_28: default 1
  //   in_30: default 1
  //   Registro D3. Registro de almacenamiento y salida.
  //   Registro de ingreso
  //   Punto 4
  //   Registro D2. Registro de almacenamiento y salida.
  //   Registro D0.Registro de almacenamiento y salida.
  //   Registro D1. Registro de almacenamiento y salida.
  //   El ejercicio nos pide 3 registros. Uno
  //   de configuración (Ingreso), uno de
  //   almacenamiento para cuando el pin
  //   de ingreso esté configurado como una
  //   entrada y un registro de control para
  //   cuando esté configurado como una
  //   salida.
  //   Primero tenemos el registro de ingreso
  //   que es igual que el visto en clase, el pin
  //   será ingresado a través de los inputs D0,
  //   D1, D2, D3, D4, cada uno este conectado 
  //   a un registro, el cual esté conectado a dos
  //   Buffer Tri-State, en este caso la conexión 
  //   sehizo con puentes nombrados iguales al
  //   input de cada registrado al cual está
  //   conectado.
  //   Se tienen dos Buffer Tri-State para cada
  //   puente, uno normal y otra con la entrada
  //   negada, para así cuando el pin que entre 
  //   sea 1, este se llama por el Tri-State normal 
  //   al registro de almacenamiento, pero si es 0,
  //   se va por el Tri-State negado y se va al 
  //   registro de control (Salida)
  //   Cuando el pin es 1,
  //   vamos al registro de
  //   almacenamiento donde
  //   tenemos un input siempre
  //   en 1, para que así el Buffer
  //   deje pasar este nivel al
  //   registro y tener el output
  //   Out #a(dependiendo del
  //   número de pin)
  //   Cuando el pin es 0,
  //   vamos al registro de control,
  //   donde tenemos un registro
  //   con un input siempre
  //   activo en el registro (a
  //   diferencia que el anterior,
  //   donde el input estaba fuera
  //   del registro), cuando el
  //   Buffer se activa, el dato pasa
  //   del registro al output
  //   Out # (dependiendo del
  //   número de registro)
  //   El enable, clock y  clear
  //   son los mismos para todos 
  //   los registros.Y cada registro 
  //   tiene su propio set.
endmodule
